# Fritzing sketch Midterm 1 Smart Room Controller (saved by Fritzing 1.0.4)
breadboards: 1

parts:
  Part1 = HX711 Weighing Sensor Module
  Load_Cell1 = Load Cell - Red/white/black/green
  OLED_I2C1 = OLED 128x64 I2C Monochrome Display
  Neopixel1 = Adafruit RBG Smart Neopixel [package="DIP (Dual Inline) [THT]"]
  Neopixel2 = Adafruit RBG Smart Neopixel [package="DIP (Dual Inline) [THT]"]
  Neopixel3 = Adafruit RBG Smart Neopixel [package="DIP (Dual Inline) [THT]"]
  U1 = ENCODER_RGB [package=encoder_led_2]  # not connected
  A1 = Particle - Photon2
  M3 = BMP280

nets:
  N1: Part1.E+, Load_Cell1.wire1
  N2: Part1.E-, Load_Cell1.wire3
  N3: Part1.A+, Load_Cell1.wire2
  N4: Part1.A-, Load_Cell1.wire4
  N5: OLED_I2C1.SDA, A1.Pin_17, M3.SDA
  N6: OLED_I2C1.SCK, A1.Pin_18, M3.SCL
  VDD: OLED_I2C1.VDD, A1.Pin_2, A1.Pin_31, M3.VIN
  GND: OLED_I2C1.GND, Neopixel1.G, Neopixel2.G, Neopixel3.G, A1.Pin_4, A1.Pin_30, M3.GND
  N7: Neopixel1.+, Neopixel2.+, Neopixel3.+, A1.Pin_26
  N8: Neopixel1.In, A1.Pin_19
  N9: Neopixel1.O, Neopixel2.In
  N10: Neopixel2.O, Neopixel3.In

custom parts:
  Load Cell - Red/white/black/green: A rectangle load cell/weighting pressure Sensor with four wires - Red, white, black, green. Normally corresponding with E+, E-, A+, A- respectively.
  ENCODER_RGB: SparkFun RGB rotary Encoder
  Particle - Photon2: The Photon 2 is a microcontroller and Wi-Fi networking developed by particle. Features: 802.11a/b/g/n Wi-Fi, 2.4 GHz and 5 GHz Integrated PCB antenna Integrated U.FL connector for external antenna Integrated RF switch BLE 5 using same antenna as Wi-Fi Realtek RTL8721DM MCU ARM Cortex M33 CPU, 200 MHz 2048 KB (2 MB) user application maximum size 3072 KB (3 MB) of RAM available to user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
  BMP280: Temperature Humidity Barometric presure Sensor, I2C
